# Fritzing sketch RTS_2 (saved by Fritzing 0.9.2b)

parts:
  Eleman1 = Arduino Uno (Rev3)
  YwRobot_Power_Supply1 = YwRobot Breadboard Power Supply [part_number=545043]
  MPU-6050 = MPU-6050 Board GY-521 [form="♀ (female)" package=THT]
  LCD1 = LCD screen
  LCM1602_IIC3 = LCM1602 IIC [part_number="LCM1602 IIC" chip_label="LCM1602 IIC" package="DIP (Dual Inline) [THT]"]
  Q1 = NPN-Transistor [package="TO92 [THT]"]
  R1 = Resistor [tolerance=±5% resistance=2k package=THT]
  C5 = Ceramic Capacitor [capacitance=100nF package="100 mil [THT, multilayer]"]
  D5 = Rectifier Diode [part_number=1N4001 package="300 mil [THT]"]
  M5 = DC Motor
  Eleman3 = HC-SR04 Ultrasonic Rangemeter
  GY2 = MPU-6050 Board GY-521 [form="♀ (female)" package=THT]  # not connected

nets:
  N1: Eleman1.A4/SDA, MPU-6050.pin4, LCM1602_IIC3.SDA
  N2: Eleman1.A5/SCL, MPU-6050.pin3, LCM1602_IIC3.SCL
  N3: Eleman1.D8, Eleman3.Trig
  N4: Eleman1.D2, MPU-6050.pin8
  N5: Eleman1.D6_PWM, R1.Pin_0
  N6: Eleman1.D7, Eleman3.Echo
  GND: Eleman1.GND, YwRobot_Power_Supply1.GND, MPU-6050.pin2, LCM1602_IIC3.GND, Q1.E, Eleman3.GND
  VCC: Eleman1.VIN, YwRobot_Power_Supply1.VCC, MPU-6050.pin1, LCM1602_IIC3.VCC, C5.1, D5.cathode, M5.pin_2, Eleman3.VCC
  VSS: LCD1.VSS, LCM1602_IIC3.VSS
  VDD: LCD1.VDD, LCM1602_IIC3.VDD
  N7: LCD1.V0, LCM1602_IIC3.V0
  N8: LCD1.RS, LCM1602_IIC3.RS
  N9: LCD1.R/W, LCM1602_IIC3.RW
  N10: LCD1.E, LCM1602_IIC3.E
  N11: LCD1.DB0, LCM1602_IIC3.D0
  N12: LCD1.DB1, LCM1602_IIC3.D1
  N13: LCD1.DB2, LCM1602_IIC3.D2
  N14: LCD1.DB3, LCM1602_IIC3.D3
  N15: LCD1.DB4, LCM1602_IIC3.D4
  N16: LCD1.DB5, LCM1602_IIC3.D5
  N17: LCD1.DB6, LCM1602_IIC3.D6
  N18: LCD1.DB7, LCM1602_IIC3.D7
  N19: LCD1.LED+, LCM1602_IIC3.A
  N20: LCD1.LED-, LCM1602_IIC3.K
  N21: Q1.B, R1.Pin_1
  N22: Q1.C, C5.0, D5.anode, M5.pin_1

notes:
  VCC
  GND
  SCL
  SDA
  XDA
  XCL
  ADD
  INT
  MPU-6050 pins
  5V
  I2C
  bus
  Amplifier

custom parts:
  YwRobot Breadboard Power Supply: The YwRobot Breadboard Power Supply (MB-V2) has two power rails; they can be 5V or 3V3. Power to the module can be provided through the female USB socket or through the A10 (female) 2.1mm power jack.
  MPU-6050 Board GY-521: Acelerometro y Giroscopio MPU-6050 Board GY-521
  LCM1602 IIC: I2C-Module to use a 1602 or 2004 LCD on with the wire.h libory Serial LCD Modul
